# Fritzing sketch infrared_wireless_remote_controller (saved by Fritzing 0.9.2b)
breadboards: 1

parts:
  Raspberry_Pi1 = Raspberry Pi 2
  R1 = Resistor [tolerance=±5% resistance=1.5k package=THT]
  R2 = Resistor [tolerance=±5% resistance=68 package=THT]
  LED1 = LED - 5mm [color="Infrared (850nm)" package="5 mm [THT]"]
  Q1 = NPN-Transistor [package="TO92 [THT]"]

nets:
  N1: Raspberry_Pi1.GPIO17, R1.Pin_0
  N2: Raspberry_Pi1.GND, Q1.E
  N3: Raspberry_Pi1.5V, R2.Pin_0
  N4: R1.Pin_1, Q1.B
  N5: R2.Pin_1, LED1.anode
  N6: LED1.cathode, Q1.C
